# Fritzing sketch Pool Controler (saved by Fritzing 0.9.3b)
breadboards: 1

parts:
  IC1 = MCP3008 8-channel 10-bit ADC [part_number=MCP3008]
  Raspberry_Pi_1 = Raspberry Pi 3 [part_number=RPI-3-V1.2]
  DS1 = DS18B20 1-Wire Temperature Sensor [part_number=DS18B20]
  R2 = Resistor [tolerance=±5% resistance=4.7k package="0603 [SMD]"]
  ELEGOO_8_Channel_DC_5V_Relay_Module = Header 10 [part_number=CA-EL-SM-005 package=1x10-2mm-smd]
  Pressure_Transducer_Sensor = Header 3 [package=1x03-1mm-ra]

nets:
  N1: IC1.no_name_yet#1, Pressure_Transducer_Sensor.3
  GND: IC1.no_name_yet#9, IC1.no_name_yet#14, Raspberry_Pi_1.GND, DS1.GND, ELEGOO_8_Channel_DC_5V_Relay_Module.10, Pressure_Transducer_Sensor.2
  N2: IC1.no_name_yet#10, Raspberry_Pi_1.GPIO8
  N3: IC1.no_name_yet#11, Raspberry_Pi_1.GPIO10
  N4: IC1.no_name_yet#12, Raspberry_Pi_1.GPIO9
  N5: IC1.no_name_yet#13, Raspberry_Pi_1.GPIO11
  3V3: IC1.no_name_yet#15, IC1.no_name_yet#16, Raspberry_Pi_1.3V3, DS1.VDD, R2.Pin_1, Pressure_Transducer_Sensor.1
  N6: Raspberry_Pi_1.GPIO4, DS1.DQ, R2.Pin_0
  N7: Raspberry_Pi_1.GPIO17, ELEGOO_8_Channel_DC_5V_Relay_Module.2
  N8: Raspberry_Pi_1.GPIO27, ELEGOO_8_Channel_DC_5V_Relay_Module.5
  N9: Raspberry_Pi_1.5V, ELEGOO_8_Channel_DC_5V_Relay_Module.1

notes:
  Multiple One Wire temperature probes
